// Logisim project practica03.circ as structural Verilog: 8 circuits, main circuit NOT
module NOT (
  input  X,
  output Not_X
);

  Transistor transistor_1 (.in(1'b1), .out(Not_X), .gate(X));
  Transistor #(.\type ("n")) transistor_2 (.in(1'b0), .out(Not_X), .gate(X));
endmodule

module OR (
  input  X,
  input  Y,
  output X_Y
);

  Transistor transistor_1 (.in(Y), .out(X_Y), .gate(X));
  Transistor #(.\type ("n")) transistor_2 (.in(X), .out(X_Y), .gate(X));
endmodule

module AND (
  input  X,
  input  Y,
  output XY
);

  Transistor transistor_1 (.in(X), .out(XY), .gate(X));
  Transistor #(.\type ("n")) transistor_2 (.in(Y), .out(XY), .gate(X));
endmodule

module Sumador1Bit (
  input  X,
  input  Y,
  input  Acarreo,
  output Suma,
  output Acarreo_2
);

  wire and_1_out, and_2_out, and_3_out, and_4_out, not_1_out, not_2_out, xor_1_out;

  not not_1 (not_1_out, Acarreo);
  not not_2 (not_2_out, xor_1_out);
  xor xor_1 (xor_1_out, X, Y);
  and and_1 (and_1_out, X, Y);
  and and_2 (and_2_out, xor_1_out, Acarreo);
  and and_3 (and_3_out, not_1_out, xor_1_out);
  and and_4 (and_4_out, not_2_out, Acarreo);
  or or_1 (Suma, and_3_out, and_4_out);
  or or_2 (Acarreo_2, and_1_out, and_2_out);

  // Notes on the sheet:
  //   Sumador de 1 bit
endmodule

module Inciso_a (
  input  X3,
  input  X2,
  input  X1,
  input  X0,
  output out_5
);

  wire and_1_xy, and_2_xy, and_3_xy, and_4_xy, minus_X2_X1_xy, minus_X3__X2_xy, minus_X3_X2_xy, not_1_not_x,
       not_2_not_x, not_3_not_x, or_1_x_y, or_2_x_y, X2__X1_xy;

  NOT not_1 (.X(X3), .Not_X(not_1_not_x));
  NOT not_2 (.X(X2), .Not_X(not_2_not_x));
  NOT not_3 (.X(X1), .Not_X(not_3_not_x));
  AND minus_X3__X2 (.X(not_1_not_x), .Y(not_2_not_x), .XY(minus_X3__X2_xy));
  AND and_1 (.X(minus_X3__X2_xy), .Y(X1), .XY(and_1_xy));
  AND minus_X3_X2 (.X(not_1_not_x), .Y(X2), .XY(minus_X3_X2_xy));
  AND and_2 (.X(minus_X3_X2_xy), .Y(X0), .XY(and_2_xy));
  AND X2__X1 (.X(X2), .Y(not_3_not_x), .XY(X2__X1_xy));
  AND minus_X2_X1 (.X(X1), .Y(not_2_not_x), .XY(minus_X2_X1_xy));
  AND and_3 (.X(X2__X1_xy), .Y(X0), .XY(and_3_xy));
  AND and_4 (.X(minus_X2_X1_xy), .Y(X0), .XY(and_4_xy));
  OR or_1 (.X(and_2_xy), .Y(and_1_xy), .X_Y(or_1_x_y));
  OR or_2 (.X(and_3_xy), .Y(and_4_xy), .X_Y(or_2_x_y));
  OR or_3 (.X(or_2_x_y), .Y(or_1_x_y), .X_Y(out_5));

  // Notes on the sheet:
  //   F(X3, X2, X1, X0)
endmodule

module Inciso_b (
  input  X2,
  input  X1,
  input  X0,
  input  X1_2,
  input  X0_2,
  input  X0_3,
  output out_7,
  output out_8,
  output out_9
);

  wire and_1_xy, and_2_xy, and_3_xy, and_4_xy, and_5_xy, not_1_not_x, not_2_not_x, not_3_not_x, not_4_not_x,
       not_5_not_x, or_2_x_y;

  NOT not_1 (.X(X2), .Not_X(not_1_not_x));
  NOT not_2 (.X(X1), .Not_X(not_2_not_x));
  NOT not_3 (.X(X0), .Not_X(not_3_not_x));
  NOT not_4 (.X(X1_2), .Not_X(not_4_not_x));
  NOT not_5 (.X(X0_2), .Not_X(not_5_not_x));
  AND and_1 (.X(not_4_not_x), .Y(X0_2), .XY(and_1_xy));
  AND and_2 (.X(X1_2), .Y(not_5_not_x), .XY(and_2_xy));
  AND and_3 (.X(not_1_not_x), .Y(X0), .XY(and_3_xy));
  AND and_4 (.X(not_1_not_x), .Y(X1), .XY(and_4_xy));
  AND and_5 (.X(X2), .Y(not_2_not_x), .XY(and_5_xy));
  OR or_1 (.X(and_2_xy), .Y(and_1_xy), .X_Y(out_8));
  OR or_2 (.X(and_4_xy), .Y(and_3_xy), .X_Y(or_2_x_y));
  OR or_3 (.X(and_5_xy), .Y(or_2_x_y), .X_Y(out_7));

  assign out_9 = X0_3;

  // Notes on the sheet:
  //   F2(X2, X1, X0)
  //   F1(X2, X1, X0)
  //   F0(X2, X1, X0)
endmodule

module Inciso_c (
  input  X2,
  input  X1,
  input  X0,
  input  X2_2,
  input  X1_2,
  input  X0_2,
  output out_7,
  output out_8
);

  wire and_1_xy, and_2_xy, and_3_xy, and_4_xy, and_5_xy, and_6_xy, and_7_xy, minus_x1__X0_xy,
       minus_x2_x1_2_xy, minus_x2_x1_xy, not_1_not_x, not_2_not_x, not_3_not_x, or_1_x_y, or_3_x_y, or_4_x_y,
       X1X0_xy;

  AND and_1 (.X(X1), .Y(X0), .XY(and_1_xy));
  NOT not_1 (.X(X2_2), .Not_X(not_1_not_x));
  NOT not_2 (.X(X1_2), .Not_X(not_2_not_x));
  NOT not_3 (.X(X0_2), .Not_X(not_3_not_x));
  AND and_2 (.X(X2), .Y(X0), .XY(and_2_xy));
  AND and_3 (.X(X2), .Y(X1), .XY(and_3_xy));
  OR or_1 (.X(and_3_xy), .Y(and_2_xy), .X_Y(or_1_x_y));
  AND minus_x1__X0 (.X(not_2_not_x), .Y(not_3_not_x), .XY(minus_x1__X0_xy));
  AND X1X0 (.X(X1_2), .Y(X0_2), .XY(X1X0_xy));
  OR or_2 (.X(and_1_xy), .Y(or_1_x_y), .X_Y(out_7));
  AND minus_x2_x1 (.X(not_1_not_x), .Y(not_2_not_x), .XY(minus_x2_x1_xy));
  AND and_4 (.X(X2_2), .Y(minus_x1__X0_xy), .XY(and_4_xy));
  AND and_5 (.X(minus_x2_x1_xy), .Y(X0_2), .XY(and_5_xy));
  AND and_6 (.X(X2_2), .Y(X1X0_xy), .XY(and_6_xy));
  AND minus_x2_x1_2 (.X(not_1_not_x), .Y(X1_2), .XY(minus_x2_x1_2_xy));
  AND and_7 (.X(minus_x2_x1_2_xy), .Y(not_3_not_x), .XY(and_7_xy));
  OR or_3 (.X(and_4_xy), .Y(and_5_xy), .X_Y(or_3_x_y));
  OR or_4 (.X(and_6_xy), .Y(and_7_xy), .X_Y(or_4_x_y));
  OR or_5 (.X(or_4_x_y), .Y(or_3_x_y), .X_Y(out_8));

  // Notes on the sheet:
  //   F1(X2, X1, X0)
  //   F0(X2, X1, X0)
endmodule

module Sumador8bits (
  input  in_1,
  input  [7:0] A,
  input  [7:0] B,
  output [7:0] A_B
);

  wire sumador1bit_1_acarreo_2, sumador1bit_2_acarreo_2, sumador1bit_3_acarreo_2, sumador1bit_4_acarreo_2,
       sumador1bit_5_acarreo_2, sumador1bit_6_acarreo_2, sumador1bit_7_acarreo_2, sumador1bit_8_acarreo_2;

  Sumador1Bit sumador1bit_1 (.X(A[0]), .Y(B[0]), .Acarreo(in_1), .Suma(A_B[0]), .Acarreo_2(sumador1bit_1_acarreo_2));
  Sumador1Bit sumador1bit_2 (
    .X(A[1]), .Y(B[1]), .Acarreo(sumador1bit_1_acarreo_2), .Suma(A_B[1]), .Acarreo_2(sumador1bit_2_acarreo_2));
  Sumador1Bit sumador1bit_3 (
    .X(A[2]), .Y(B[2]), .Acarreo(sumador1bit_2_acarreo_2), .Suma(A_B[2]), .Acarreo_2(sumador1bit_3_acarreo_2));
  Sumador1Bit sumador1bit_4 (
    .X(A[3]), .Y(B[3]), .Acarreo(sumador1bit_3_acarreo_2), .Suma(A_B[3]), .Acarreo_2(sumador1bit_4_acarreo_2));
  Sumador1Bit sumador1bit_5 (
    .X(A[4]), .Y(B[4]), .Acarreo(sumador1bit_4_acarreo_2), .Suma(A_B[4]), .Acarreo_2(sumador1bit_5_acarreo_2));
  Sumador1Bit sumador1bit_6 (
    .X(A[5]), .Y(B[5]), .Acarreo(sumador1bit_5_acarreo_2), .Suma(A_B[5]), .Acarreo_2(sumador1bit_6_acarreo_2));
  Sumador1Bit sumador1bit_7 (
    .X(A[6]), .Y(B[6]), .Acarreo(sumador1bit_6_acarreo_2), .Suma(A_B[6]), .Acarreo_2(sumador1bit_7_acarreo_2));
  Sumador1Bit sumador1bit_8 (
    .X(A[7]), .Y(B[7]), .Acarreo(sumador1bit_7_acarreo_2), .Suma(A_B[7]), .Acarreo_2(sumador1bit_8_acarreo_2));
  // Probe on sumador1bit_8_acarreo_2

  // Notes on the sheet:
  //   Sumador de 8 bits
endmodule
