// Logisim project alu.circ as structural Verilog: 7 circuits, main circuit Sumador 1-Bit
module Sumador_1_Bit (
  input  Acarreo_Entrada,
  input  A,
  input  B,
  output Salida,
  output Acarreo_Salida
);

  wire and_1_out, and_2_out, operador_xor_1_salida;

  and and_1 (and_1_out, A, B);
  Operador_XOR operador_xor_1 (.A(A), .B(B), .Salida(operador_xor_1_salida));
  or or_1 (Acarreo_Salida, and_1_out, and_2_out);
  and and_2 (and_2_out, Acarreo_Entrada, operador_xor_1_salida);
  Operador_XOR operador_xor_2 (.A(operador_xor_1_salida), .B(Acarreo_Entrada), .Salida(Salida));

  // Notes on the sheet:
  //   Input:
  //   Output:
  //   - Dos entradas A y B de 1 bit
  //   - Un acarreo de entrada de 1 bit
  //   - La suma de 1 bit
  //   - Un acarreo de salida de 1 bit
  //   Sumador Completo para entradas de 1-Bit
endmodule

module Operador_XOR (
  input  A,
  input  B,
  output Salida
);

  wire not_1_out, not_2_out, or_1_out, or_2_out;

  not not_1 (not_1_out, A);
  not not_2 (not_2_out, B);
  or or_1 (or_1_out, A, B);
  or or_2 (or_2_out, not_1_out, not_2_out);
  and and_1 (Salida, or_1_out, or_2_out);

  // Notes on the sheet:
  //   Operador XOR
  //   ¬A
  //   ¬B
  //   A v B
  //   ¬A v ¬B
  //   (A v B) ^ (¬A v ¬B)
endmodule

module Ejercicio_1 (
  input  Acarreo_Entrada,
  input  [2:0] \Operación ,
  input  A,
  input  B,
  output Salida,
  output Acarreo_Salida
);

  wire and_1_out, not_1_out, or_1_out, sumador_1_bit_1_salida;

  and and_1 (and_1_out, A, B);
  not not_1 (not_1_out, A);
  or or_1 (or_1_out, A, B);
  Sumador_1_Bit sumador_1_bit_1 (
    .Acarreo_Entrada(Acarreo_Entrada), .Salida(sumador_1_bit_1_salida), .Acarreo_Salida(Acarreo_Salida),
    .A(A), .B(B));
  Multiplexer #(.select(3), .enable("false")) multiplexer_1 (
    .in0(and_1_out), .in1(or_1_out), .in2(not_1_out), .in3(sumador_1_bit_1_salida),
    .in4(sumador_1_bit_1_salida), .in5(sumador_1_bit_1_salida), .in6(sumador_1_bit_1_salida),
    .in7(sumador_1_bit_1_salida), .out(Salida), .sel(\Operación ));

  // Notes on the sheet:
  //   Ejercicio 1:
  //   - And
  //   - Or
  //   - Not
  //   - Adición
  //   Unidad Aritmético-Lógica (ALU) de 1-Bit con operaciones:
  //   AND
  //   OR
  //   SUMA
  //   Códigos de las
  //   Operaciones
  //   000 - AND
  //   001 - OR
  //   010 - NOT
  //   110 - Adición
endmodule

module Ejercicio_2 (
  input  [2:0] \Operación ,
  input  Acarreo_Entrada,
  input  [7:0] A,
  input  [7:0] B,
  output [7:0] Salida,
  output Desbordamiento
);

  wire and_2_out, ejercicio_1_1_acarreo_salida, ejercicio_1_2_acarreo_salida, ejercicio_1_3_acarreo_salida,
       ejercicio_1_4_acarreo_salida, ejercicio_1_5_acarreo_salida, ejercicio_1_6_acarreo_salida,
       ejercicio_1_7_acarreo_salida, ejercicio_1_8_acarreo_salida, not_1_out;

  and and_1 (Desbordamiento, ejercicio_1_8_acarreo_salida, and_2_out);
  Ejercicio_1 ejercicio_1_1 (
    .A(A[0]), .B(B[0]), .Salida(Salida[0]), .Acarreo_Entrada(Acarreo_Entrada), .\Operación (\Operación ),
    .Acarreo_Salida(ejercicio_1_1_acarreo_salida));
  Ejercicio_1 ejercicio_1_2 (
    .A(A[1]), .B(B[1]), .Salida(Salida[1]), .Acarreo_Entrada(ejercicio_1_1_acarreo_salida),
    .\Operación (\Operación ), .Acarreo_Salida(ejercicio_1_2_acarreo_salida));
  Ejercicio_1 ejercicio_1_3 (
    .A(A[2]), .B(B[2]), .Salida(Salida[2]), .Acarreo_Entrada(ejercicio_1_2_acarreo_salida),
    .\Operación (\Operación ), .Acarreo_Salida(ejercicio_1_3_acarreo_salida));
  Ejercicio_1 ejercicio_1_4 (
    .A(A[3]), .B(B[3]), .Salida(Salida[3]), .Acarreo_Entrada(ejercicio_1_3_acarreo_salida),
    .\Operación (\Operación ), .Acarreo_Salida(ejercicio_1_4_acarreo_salida));
  Ejercicio_1 ejercicio_1_5 (
    .A(A[4]), .B(B[4]), .Salida(Salida[4]), .Acarreo_Entrada(ejercicio_1_4_acarreo_salida),
    .\Operación (\Operación ), .Acarreo_Salida(ejercicio_1_5_acarreo_salida));
  Ejercicio_1 ejercicio_1_6 (
    .A(A[5]), .B(B[5]), .Salida(Salida[5]), .Acarreo_Entrada(ejercicio_1_5_acarreo_salida),
    .\Operación (\Operación ), .Acarreo_Salida(ejercicio_1_6_acarreo_salida));
  Ejercicio_1 ejercicio_1_7 (
    .A(A[6]), .B(B[6]), .Salida(Salida[6]), .Acarreo_Entrada(ejercicio_1_6_acarreo_salida),
    .\Operación (\Operación ), .Acarreo_Salida(ejercicio_1_7_acarreo_salida));
  Ejercicio_1 ejercicio_1_8 (
    .A(A[7]), .B(B[7]), .Salida(Salida[7]), .Acarreo_Entrada(ejercicio_1_7_acarreo_salida),
    .\Operación (\Operación ), .Acarreo_Salida(ejercicio_1_8_acarreo_salida));
  not not_1 (not_1_out, \Operación [0]);
  and and_2 (and_2_out, \Operación [2], \Operación [1], not_1_out);

  // Other names for the same wires on the sheet: D[2:0] = \Operación 

  // Notes on the sheet:
  //   - And
  //   - Or
  //   - Not
  //   - Adición
  //   Ejercicio 2:
  //   Unidad Aritmético-Lógica (ALU) de 8-Bits con operaciones:
  //   Códigos de las
  //   Operaciones
  //   000 - AND
  //   001 - OR
  //   010 - NOT
  //   110 - Adición
endmodule

module Ejercicio_3 (
  input  [2:0] \Operación ,
  input  [7:0] A,
  input  [7:0] B,
  output [7:0] Salida,
  output Desbordamiento
);

  wire and_2_out, and_3_out, ejercicio_1_1_acarreo_salida, ejercicio_1_2_acarreo_salida,
       ejercicio_1_3_acarreo_salida, ejercicio_1_4_acarreo_salida, ejercicio_1_5_acarreo_salida,
       ejercicio_1_6_acarreo_salida, ejercicio_1_7_acarreo_salida, ejercicio_1_8_acarreo_salida, not_2_out;
  wire [7:0] multiplexer_1_out, not_1_out;

  Multiplexer #(.width(8), .enable("false")) multiplexer_1 (
    .in0(B), .in1(not_1_out), .out(multiplexer_1_out), .sel(and_2_out));
  assign not_1_out = ~B;  // NOT_Gate not_1, 8 bits wide
  and and_1 (Desbordamiento, ejercicio_1_8_acarreo_salida, and_3_out);
  and and_2 (and_2_out, \Operación [0], \Operación [1], \Operación [2]);
  Ejercicio_1 ejercicio_1_1 (
    .A(A[0]), .B(multiplexer_1_out[0]), .Salida(Salida[0]), .Acarreo_Entrada(and_2_out),
    .\Operación (\Operación ), .Acarreo_Salida(ejercicio_1_1_acarreo_salida));
  Ejercicio_1 ejercicio_1_2 (
    .A(A[1]), .B(multiplexer_1_out[1]), .Salida(Salida[1]), .Acarreo_Entrada(ejercicio_1_1_acarreo_salida),
    .\Operación (\Operación ), .Acarreo_Salida(ejercicio_1_2_acarreo_salida));
  Ejercicio_1 ejercicio_1_3 (
    .A(A[2]), .B(multiplexer_1_out[2]), .Salida(Salida[2]), .Acarreo_Entrada(ejercicio_1_2_acarreo_salida),
    .\Operación (\Operación ), .Acarreo_Salida(ejercicio_1_3_acarreo_salida));
  Ejercicio_1 ejercicio_1_4 (
    .A(A[3]), .B(multiplexer_1_out[3]), .Salida(Salida[3]), .Acarreo_Entrada(ejercicio_1_3_acarreo_salida),
    .\Operación (\Operación ), .Acarreo_Salida(ejercicio_1_4_acarreo_salida));
  Ejercicio_1 ejercicio_1_5 (
    .A(A[4]), .B(multiplexer_1_out[4]), .Salida(Salida[4]), .Acarreo_Entrada(ejercicio_1_4_acarreo_salida),
    .\Operación (\Operación ), .Acarreo_Salida(ejercicio_1_5_acarreo_salida));
  Ejercicio_1 ejercicio_1_6 (
    .A(A[5]), .B(multiplexer_1_out[5]), .Salida(Salida[5]), .Acarreo_Entrada(ejercicio_1_5_acarreo_salida),
    .\Operación (\Operación ), .Acarreo_Salida(ejercicio_1_6_acarreo_salida));
  Ejercicio_1 ejercicio_1_7 (
    .A(A[6]), .B(multiplexer_1_out[6]), .Salida(Salida[6]), .Acarreo_Entrada(ejercicio_1_6_acarreo_salida),
    .\Operación (\Operación ), .Acarreo_Salida(ejercicio_1_7_acarreo_salida));
  Ejercicio_1 ejercicio_1_8 (
    .A(A[7]), .B(multiplexer_1_out[7]), .Salida(Salida[7]), .Acarreo_Entrada(ejercicio_1_7_acarreo_salida),
    .\Operación (\Operación ), .Acarreo_Salida(ejercicio_1_8_acarreo_salida));
  not not_2 (not_2_out, \Operación [0]);
  and and_3 (and_3_out, \Operación [2], \Operación [1], not_2_out);

  // Other names for the same wires on the sheet: D[2:0] = \Operación 

  // Notes on the sheet:
  //   - And
  //   - Or
  //   - Not
  //   - Adición
  //   Ejercicio 3:
  //   - Sustracción
  //   Unidad Aritmético-Lógica (ALU) de 8-Bits con operaciones:
  //   001 - OR
  //   Códigos de las
  //   Operaciones
  //   000 - AND
  //   010 - NOT
  //   110 - Adición
  //   111 - Sustracción
endmodule

module Ejercicio_4 (
  input  [2:0] \Operación ,
  input  [7:0] A,
  input  [7:0] B,
  output [7:0] Salida,
  output Desbordamiento
);

  wire and_2_out, and_3_out, and_4_out, ejercicio_1_1_acarreo_salida, ejercicio_1_1_salida,
       ejercicio_1_2_acarreo_salida, ejercicio_1_3_acarreo_salida, ejercicio_1_4_acarreo_salida,
       ejercicio_1_5_acarreo_salida, ejercicio_1_6_acarreo_salida, ejercicio_1_7_acarreo_salida,
       ejercicio_1_8_acarreo_salida, not_2_out, not_3_out, or_1_out, or_2_out, or_3_out, tunnel_t, tunnel_t_t;
  wire [7:0] multiplexer_1_out, not_1_out;

  Multiplexer #(.width(8), .enable("false")) multiplexer_1 (
    .in0(B), .in1(not_1_out), .out(multiplexer_1_out), .sel(or_1_out));
  assign not_1_out = ~B;  // NOT_Gate not_1, 8 bits wide
  and and_1 (Desbordamiento, ejercicio_1_8_acarreo_salida, and_4_out);
  and and_2 (and_2_out, not_2_out, \Operación [2]);
  or or_1 (or_1_out, and_2_out, and_3_out);
  and and_3 (and_3_out, \Operación [1], \Operación [0]);
  Ejercicio_1 ejercicio_1_1 (
    .A(A[0]), .B(multiplexer_1_out[0]), .Salida(ejercicio_1_1_salida), .Acarreo_Entrada(or_1_out),
    .\Operación (\Operación ), .Acarreo_Salida(ejercicio_1_1_acarreo_salida));
  Ejercicio_1 ejercicio_1_2 (
    .A(A[1]), .B(multiplexer_1_out[1]), .Salida(Salida[1]), .Acarreo_Entrada(ejercicio_1_1_acarreo_salida),
    .\Operación (\Operación ), .Acarreo_Salida(ejercicio_1_2_acarreo_salida));
  Ejercicio_1 ejercicio_1_3 (
    .A(A[2]), .B(multiplexer_1_out[2]), .Salida(Salida[2]), .Acarreo_Entrada(ejercicio_1_2_acarreo_salida),
    .\Operación (\Operación ), .Acarreo_Salida(ejercicio_1_3_acarreo_salida));
  Ejercicio_1 ejercicio_1_4 (
    .A(A[3]), .B(multiplexer_1_out[3]), .Salida(Salida[3]), .Acarreo_Entrada(ejercicio_1_3_acarreo_salida),
    .\Operación (\Operación ), .Acarreo_Salida(ejercicio_1_4_acarreo_salida));
  Ejercicio_1 ejercicio_1_5 (
    .A(A[4]), .B(multiplexer_1_out[4]), .Salida(Salida[4]), .Acarreo_Entrada(ejercicio_1_4_acarreo_salida),
    .\Operación (\Operación ), .Acarreo_Salida(ejercicio_1_5_acarreo_salida));
  Ejercicio_1 ejercicio_1_6 (
    .A(A[5]), .B(multiplexer_1_out[5]), .Salida(Salida[5]), .Acarreo_Entrada(ejercicio_1_5_acarreo_salida),
    .\Operación (\Operación ), .Acarreo_Salida(ejercicio_1_6_acarreo_salida));
  Ejercicio_1 ejercicio_1_7 (
    .A(A[6]), .B(multiplexer_1_out[6]), .Salida(Salida[6]), .Acarreo_Entrada(ejercicio_1_6_acarreo_salida),
    .\Operación (\Operación ), .Acarreo_Salida(ejercicio_1_7_acarreo_salida));
  Ejercicio_1 ejercicio_1_8 (
    .A(A[7]), .B(multiplexer_1_out[7]), .Salida(Salida[7]), .Acarreo_Entrada(ejercicio_1_7_acarreo_salida),
    .\Operación (\Operación ), .Acarreo_Salida(ejercicio_1_8_acarreo_salida));
  not not_2 (not_2_out, \Operación [1]);
  not not_3 (not_3_out, \Operación [0]);
  and and_4 (and_4_out, \Operación [2], \Operación [1], not_3_out);
  not not_4 (tunnel_t, or_2_out);
  or or_2 (or_2_out, ejercicio_1_1_salida, Salida[1], Salida[2], Salida[3], Salida[4], Salida[5], Salida[6], Salida[7]);
  Multiplexer #(.select(3), .enable("false")) multiplexer_2 (
    .in0(ejercicio_1_1_salida), .in1(ejercicio_1_1_salida), .in2(ejercicio_1_1_salida), .in3(Salida[7]),
    .in4(tunnel_t_t), .in5(tunnel_t), .in6(ejercicio_1_1_salida), .in7(ejercicio_1_1_salida),
    .out(Salida[0]), .sel(\Operación ));
  or or_3 (or_3_out, Salida[7], tunnel_t);
  not not_5 (tunnel_t_t, or_3_out);

  // Other names for the same wires on the sheet: D[2:0] = \Operación ; P = \Operación [0]; tunnel = Salida[7]

  // Notes on the sheet:
  //   Ejercicio 4:
  //   - And
  //   - Or
  //   - Not
  //   - Adición
  //   - Sustracción
  //   Notas:
  //   - Comparación
  //   Si es 0, entonces la premisa es falsa. Si es 1, es verdadera.
  //   Unidad Aritmético-Lógica (ALU) de 8-Bits con operaciones:
  //   En las comparaciones, el Bit Menos Significativo nos dice el resultado:
  //   Si hay Overflow en la resta, el resultado de las comparaciones puede no ser correcto.
  //   Códigos de las
  //   000 - AND
  //   001 - OR
  //   010 - NOT
  //   101 - Igualdad
  //   110 - Adición
  //   Operaciones
  //   011 - Menor que
  //   100 - Mayor que
  //   111 - Sustracción
endmodule

module Ejercicio_5 (
  input  [2:0] \Operación ,
  input  [7:0] A,
  input  [7:0] B,
  output [7:0] Resultado,
  output Desbordamiento
);

  Ejercicio_4 ejercicio_4_1 (
    .A(A), .B(B), .Desbordamiento(Desbordamiento), .Salida(Resultado), .\Operación (\Operación ));

  // Notes on the sheet:
  //   Notas:
  //   Si es 0, entonces la premisa es falsa. Si es 1, es verdadera.
  //   En las comparaciones, el Bit Menos Significativo nos dice el resultado:
  //   Si hay Overflow en la resta, el resultado de las comparaciones puede no ser correcto.
  //   Organización y Arquitectura de Computadoras [2020-1]
  //   Facultad de Ciencias - UNAM
  //   Práctica #04: Unidad Aritmético-Lógica
  //   Códigos de las
  //   Operaciones
  //   000 - AND
  //   001 - OR
  //   010 - NOT
  //   011 - Menor que
  //   100 - Mayor que
  //   101 - Igualdad
  //   110 - Adición
  //   111 - Sustracción
  //   Autores
  //   Johann Ramón Gordillo Guzmán
  //   José Jhovan Gallardo Valdez
endmodule
