// Logisim project circuitos.circ as structural Verilog: 10 circuits, main circuit Ejercicio 2 - Registro 1-Bit
module Ejercicio_1___Automata_D (
  input  Entrada,
  output Salida
);

  wire and_1_out, and_2_out, and_3_out, and_4_out, ck, not_1_out, not_2_out, not_3_out, not_4_out, or_1_out,
       or_2_out, or_3_out;
  wire [1:0] Q1_q;

  Clock clock_1 (.out(ck));
  not not_1 (not_1_out, Q1_q[1]);
  not not_2 (not_2_out, Entrada);
  not not_3 (not_3_out, Q1_q[0]);
  not not_4 (not_4_out, Entrada);
  and and_1 (and_1_out, not_1_out, Entrada);
  or or_1 (or_1_out, and_1_out, and_2_out);
  and and_2 (and_2_out, Q1_q[1], not_2_out);
  and and_3 (and_3_out, Q1_q[0], Entrada);
  or or_2 (or_2_out, and_3_out, and_4_out);
  and and_4 (and_4_out, not_3_out, not_4_out);
  D_Flip_Flop Q0 (.clk(ck), .D(or_1_out), .Q(Q1_q[1]));  // open: Qn, preset, en, reset
  D_Flip_Flop Q1 (.clk(ck), .D(or_2_out), .Q(Q1_q[0]));  // open: Qn, preset, en, reset
  or or_3 (or_3_out, Q1_q[1], Q1_q[0]);
  // Probe on Q1_q
  not not_5 (Salida, or_3_out);

  // Notes on the sheet:
  //   Autómata diseñado con flip-flops de tipo D
endmodule

module Ejercicio_1___Automata_JK (
  input  Entrada,
  output Salida
);

  wire Ck, not_1_out, or_1_out;
  wire [1:0] Q1_q;

  Clock u_Ck (.out(Ck));
  not not_1 (not_1_out, Entrada);
  J_K_Flip_Flop Q1 (.J(not_1_out), .clk(Ck), .K(not_1_out), .Q(Q1_q[0]));  // open: Qn, preset, en, reset
  J_K_Flip_Flop Q0 (.J(Entrada), .clk(Ck), .K(Entrada), .Q(Q1_q[1]));  // open: Qn, preset, en, reset
  not not_2 (Salida, or_1_out);
  or or_1 (or_1_out, Q1_q[0], Q1_q[1]);
  // Probe on Q1_q

  // Notes on the sheet:
  //   Autómata diseñado con flip-flops de tipo JK
endmodule

module Ejercicio_2___Registro_1_Bit (
  input  Ck,
  input  In,
  input  Enable,
  output Out,
  output out_5
);

  wire not_1_out;

  not not_1 (not_1_out, In);
  S_R_Flip_Flop s_r_ff_1 (.S(In), .clk(Ck), .R(not_1_out), .Q(Out), .Qn(out_5), .en(Enable));  // open: preset, reset

  // Notes on the sheet:
  //   Registro de 1-Bit
  //   0 - Lectura 
  //   1 - Escritura
endmodule

module Ejercicio_3___Registro_8_Bits (
  input  Ck,
  input  [7:0] In,
  input  Enable,
  output [7:0] Out
);

  Ejercicio_2___Registro_1_Bit ejercicio_2_registro_1_bit_1 (
    .In(In[0]), .Out(Out[0]), .Ck(Ck), .Enable(Enable));  // open: out_5
  Ejercicio_2___Registro_1_Bit ejercicio_2_registro_1_bit_2 (
    .In(In[1]), .Out(Out[1]), .Ck(Ck), .Enable(Enable));  // open: out_5
  Ejercicio_2___Registro_1_Bit ejercicio_2_registro_1_bit_3 (
    .In(In[2]), .Out(Out[2]), .Ck(Ck), .Enable(Enable));  // open: out_5
  Ejercicio_2___Registro_1_Bit ejercicio_2_registro_1_bit_4 (
    .In(In[3]), .Out(Out[3]), .Ck(Ck), .Enable(Enable));  // open: out_5
  Ejercicio_2___Registro_1_Bit ejercicio_2_registro_1_bit_5 (
    .In(In[4]), .Out(Out[4]), .Ck(Ck), .Enable(Enable));  // open: out_5
  Ejercicio_2___Registro_1_Bit ejercicio_2_registro_1_bit_6 (
    .In(In[5]), .Out(Out[5]), .Ck(Ck), .Enable(Enable));  // open: out_5
  Ejercicio_2___Registro_1_Bit ejercicio_2_registro_1_bit_7 (
    .In(In[6]), .Out(Out[6]), .Ck(Ck), .Enable(Enable));  // open: out_5
  Ejercicio_2___Registro_1_Bit ejercicio_2_registro_1_bit_8 (
    .In(In[7]), .Out(Out[7]), .Ck(Ck), .Enable(Enable));  // open: out_5

  // Notes on the sheet:
  //   Registro de 8-Bits
endmodule

module Ejercicio_4___Banco_de_registros (
  input  Escribir,
  input  [1:0] Leer_Registro_1,
  input  [1:0] Leer_Registro_2,
  input  [1:0] Escribir_Registro,
  input  [7:0] Escribir_Datos,
  output [7:0] Leer_Datos_1,
  output [7:0] Leer_Datos_2
);

  wire decoder_1_out0, decoder_1_out1, decoder_1_out2, decoder_1_out3;
  wire [7:0] ejercicio_3_registro_8_bits_1_out, ejercicio_3_registro_8_bits_2_out,
       ejercicio_3_registro_8_bits_3_out, ejercicio_3_registro_8_bits_4_out;

  Decoder #(.select(2), .enable("false")) decoder_1 (
    .out0(decoder_1_out0), .out1(decoder_1_out1), .out2(decoder_1_out2), .out3(decoder_1_out3),
    .sel(Escribir_Registro));
  Ejercicio_3___Registro_8_Bits ejercicio_3_registro_8_bits_1 (
    .In(Escribir_Datos), .Out(ejercicio_3_registro_8_bits_1_out), .Ck(Escribir), .Enable(decoder_1_out0));
  Ejercicio_3___Registro_8_Bits ejercicio_3_registro_8_bits_2 (
    .In(Escribir_Datos), .Out(ejercicio_3_registro_8_bits_2_out), .Ck(Escribir), .Enable(decoder_1_out1));
  Ejercicio_3___Registro_8_Bits ejercicio_3_registro_8_bits_3 (
    .In(Escribir_Datos), .Out(ejercicio_3_registro_8_bits_3_out), .Ck(Escribir), .Enable(decoder_1_out2));
  Ejercicio_3___Registro_8_Bits ejercicio_3_registro_8_bits_4 (
    .In(Escribir_Datos), .Out(ejercicio_3_registro_8_bits_4_out), .Ck(Escribir), .Enable(decoder_1_out3));
  Multiplexer #(.select(2), .width(8), .enable("false")) multiplexer_1 (
    .in0(ejercicio_3_registro_8_bits_1_out), .in1(ejercicio_3_registro_8_bits_2_out),
    .in2(ejercicio_3_registro_8_bits_3_out), .in3(ejercicio_3_registro_8_bits_4_out), .out(Leer_Datos_1),
    .sel(Leer_Registro_1));
  Multiplexer #(.select(2), .width(8), .enable("false")) multiplexer_2 (
    .in0(ejercicio_3_registro_8_bits_1_out), .in1(ejercicio_3_registro_8_bits_2_out),
    .in2(ejercicio_3_registro_8_bits_3_out), .in3(ejercicio_3_registro_8_bits_4_out), .out(Leer_Datos_2),
    .sel(Leer_Registro_2));

  // Notes on the sheet:
  //   Banco de Registros
endmodule

module Ejercicio_5___Banco_ALU (
  input  [1:0] Leer_Registro_1,
  input  [2:0] \Operación ,
  input  [1:0] Leer_Registro_2,
  input  [1:0] Escribir_Registro,
  input  Segundo_Operando,
  input  Escribir,
  input  [5:0] Inmediato,
  output [7:0] Resultado,
  output Desbordamiento
);

  wire [7:0] ejercicio_4_banco_de_registros_1_leer_datos_1, ejercicio_4_banco_de_registros_1_leer_datos_2,
       multiplexer_1_out;

  Multiplexer #(.width(8), .enable("false")) multiplexer_1 (
    .in0(Resultado), .in1({2'b00, Inmediato}), .out(multiplexer_1_out), .sel(Segundo_Operando));
  Ejercicio_4___Banco_de_registros ejercicio_4_banco_de_registros_1 (
    .Leer_Registro_1(Leer_Registro_1), .Leer_Registro_2(Leer_Registro_2), .Escribir(Escribir),
    .Escribir_Registro(Escribir_Registro), .Escribir_Datos(multiplexer_1_out),
    .Leer_Datos_2(ejercicio_4_banco_de_registros_1_leer_datos_2),
    .Leer_Datos_1(ejercicio_4_banco_de_registros_1_leer_datos_1));
  ALU_8_Bits alu_8_bits_1 (
    .A(ejercicio_4_banco_de_registros_1_leer_datos_1), .B(ejercicio_4_banco_de_registros_1_leer_datos_2),
    .Desbordamiento(Desbordamiento), .\Operación (\Operación ), .Salida(Resultado));

  // Notes on the sheet:
  //   Notas:
  //   Notas:
  //   Si es 0, entonces la premisa es falsa. Si es 1, es verdadera.
  //   Si es 0, entonces la premisa es falsa. Si es 1, es verdadera.
  //   En las comparaciones, el Bit Menos Significativo nos dice el resultado:
  //   Si hay Overflow en la resta, el resultado de las comparaciones puede no ser correcto.
  //   En las comparaciones, el Bit Menos Significativo nos dice el resultado:
  //   Si hay Overflow en la resta, el resultado de las comparaciones puede no ser correcto.
  //   Organización y Arquitectura de Computadoras [2020-1]
  //   Facultad de Ciencias - UNAM
  //   Práctica #05: Lógica Secuencial
  //   Autores
  //   Johann Ramón Gordillo Guzmán
  //   José Jhovan Gallardo Valdez
  //   Autores
  //   Johann Ramón Gordillo Guzmán
  //   José Jhovan Gallardo Valdez
  //   Códigos de las
  //   Operaciones
  //   000 - AND
  //   001 - OR
  //   010 - NOT
  //   011 - Menor que
  //   100 - Mayor que
  //   101 - Igualdad
  //   110 - Adición
  //   111 - Sustracción
endmodule

module Operador_XOR (
  input  A,
  input  B,
  output Salida
);

  wire not_1_out, not_2_out, or_1_out, or_2_out;

  not not_1 (not_1_out, A);
  not not_2 (not_2_out, B);
  or or_1 (or_1_out, A, B);
  or or_2 (or_2_out, not_1_out, not_2_out);
  and and_1 (Salida, or_1_out, or_2_out);

  // Notes on the sheet:
  //   Operador XOR
  //   ¬A
  //   ¬B
  //   A v B
  //   ¬A v ¬B
  //   (A v B) ^ (¬A v ¬B)
endmodule

module Sumador_1_Bit (
  input  Acarreo_Entrada,
  input  A,
  input  B,
  output Salida,
  output Acarreo_Salida
);

  wire and_1_out, and_2_out, operador_xor_1_salida;

  and and_1 (and_1_out, A, B);
  Operador_XOR operador_xor_1 (.A(A), .B(B), .Salida(operador_xor_1_salida));
  or or_1 (Acarreo_Salida, and_1_out, and_2_out);
  and and_2 (and_2_out, Acarreo_Entrada, operador_xor_1_salida);
  Operador_XOR operador_xor_2 (.A(operador_xor_1_salida), .B(Acarreo_Entrada), .Salida(Salida));

  // Notes on the sheet:
  //   Input:
  //   Output:
  //   - Dos entradas A y B de 1 bit
  //   - Un acarreo de entrada de 1 bit
  //   - La suma de 1 bit
  //   - Un acarreo de salida de 1 bit
  //   Sumador Completo para entradas de 1-Bit
endmodule

module ALU_1_Bit (
  input  Acarreo_Entrada,
  input  [2:0] \Operación ,
  input  A,
  input  B,
  output Salida,
  output Acarreo_Salida
);

  wire and_1_out, not_1_out, or_1_out, sumador_1_bit_1_salida;

  and and_1 (and_1_out, A, B);
  not not_1 (not_1_out, A);
  or or_1 (or_1_out, A, B);
  Sumador_1_Bit sumador_1_bit_1 (
    .A(A), .B(B), .Salida(sumador_1_bit_1_salida), .Acarreo_Entrada(Acarreo_Entrada),
    .Acarreo_Salida(Acarreo_Salida));
  Multiplexer #(.select(3), .enable("false")) multiplexer_1 (
    .in0(and_1_out), .in1(or_1_out), .in2(not_1_out), .in3(sumador_1_bit_1_salida),
    .in4(sumador_1_bit_1_salida), .in5(sumador_1_bit_1_salida), .in6(sumador_1_bit_1_salida),
    .in7(sumador_1_bit_1_salida), .out(Salida), .sel(\Operación ));

  // Notes on the sheet:
  //   - And
  //   - Or
  //   - Not
  //   - Adición
  //   Unidad Aritmético-Lógica (ALU) de 1-Bit con operaciones:
  //   AND
  //   OR
  //   SUMA
  //   Códigos de las
  //   Operaciones
  //   000 - AND
  //   001 - OR
  //   010 - NOT
  //   110 - Adición
endmodule

module ALU_8_Bits (
  input  [2:0] \Operación ,
  input  [7:0] A,
  input  [7:0] B,
  output [7:0] Salida,
  output Desbordamiento
);

  wire alu_1_bit_1_acarreo_salida, alu_1_bit_1_salida, alu_1_bit_2_acarreo_salida,
       alu_1_bit_3_acarreo_salida, alu_1_bit_4_acarreo_salida, alu_1_bit_5_acarreo_salida,
       alu_1_bit_6_acarreo_salida, alu_1_bit_7_acarreo_salida, alu_1_bit_8_acarreo_salida, and_2_out,
       and_3_out, and_4_out, not_2_out, not_3_out, or_1_out, or_2_out, or_3_out, tunnel_t, tunnel_t_t;
  wire [7:0] multiplexer_1_out, not_1_out;

  assign not_1_out = ~B;  // NOT_Gate not_1, 8 bits wide
  Multiplexer #(.width(8), .enable("false")) multiplexer_1 (
    .in0(B), .in1(not_1_out), .out(multiplexer_1_out), .sel(or_1_out));
  and and_1 (Desbordamiento, alu_1_bit_8_acarreo_salida, and_4_out);
  or or_1 (or_1_out, and_2_out, and_3_out);
  not not_2 (not_2_out, \Operación [1]);
  and and_2 (and_2_out, not_2_out, \Operación [2]);
  and and_3 (and_3_out, \Operación [1], \Operación [0]);
  ALU_1_Bit alu_1_bit_1 (
    .A(A[0]), .B(multiplexer_1_out[0]), .Salida(alu_1_bit_1_salida), .Acarreo_Entrada(or_1_out),
    .\Operación (\Operación ), .Acarreo_Salida(alu_1_bit_1_acarreo_salida));
  ALU_1_Bit alu_1_bit_2 (
    .A(A[1]), .B(multiplexer_1_out[1]), .Salida(Salida[1]), .Acarreo_Entrada(alu_1_bit_1_acarreo_salida),
    .\Operación (\Operación ), .Acarreo_Salida(alu_1_bit_2_acarreo_salida));
  ALU_1_Bit alu_1_bit_3 (
    .A(A[2]), .B(multiplexer_1_out[2]), .Salida(Salida[2]), .Acarreo_Entrada(alu_1_bit_2_acarreo_salida),
    .\Operación (\Operación ), .Acarreo_Salida(alu_1_bit_3_acarreo_salida));
  ALU_1_Bit alu_1_bit_4 (
    .A(A[3]), .B(multiplexer_1_out[3]), .Salida(Salida[3]), .Acarreo_Entrada(alu_1_bit_3_acarreo_salida),
    .\Operación (\Operación ), .Acarreo_Salida(alu_1_bit_4_acarreo_salida));
  ALU_1_Bit alu_1_bit_5 (
    .A(A[4]), .B(multiplexer_1_out[4]), .Salida(Salida[4]), .Acarreo_Entrada(alu_1_bit_4_acarreo_salida),
    .\Operación (\Operación ), .Acarreo_Salida(alu_1_bit_5_acarreo_salida));
  ALU_1_Bit alu_1_bit_6 (
    .A(A[5]), .B(multiplexer_1_out[5]), .Salida(Salida[5]), .Acarreo_Entrada(alu_1_bit_5_acarreo_salida),
    .\Operación (\Operación ), .Acarreo_Salida(alu_1_bit_6_acarreo_salida));
  ALU_1_Bit alu_1_bit_7 (
    .A(A[6]), .B(multiplexer_1_out[6]), .Salida(Salida[6]), .Acarreo_Entrada(alu_1_bit_6_acarreo_salida),
    .\Operación (\Operación ), .Acarreo_Salida(alu_1_bit_7_acarreo_salida));
  ALU_1_Bit alu_1_bit_8 (
    .A(A[7]), .B(multiplexer_1_out[7]), .Salida(Salida[7]), .Acarreo_Entrada(alu_1_bit_7_acarreo_salida),
    .\Operación (\Operación ), .Acarreo_Salida(alu_1_bit_8_acarreo_salida));
  not not_3 (not_3_out, \Operación [0]);
  and and_4 (and_4_out, \Operación [2], \Operación [1], not_3_out);
  or or_2 (or_2_out, alu_1_bit_1_salida, Salida[1], Salida[2], Salida[3], Salida[4], Salida[5], Salida[6], Salida[7]);
  not not_4 (tunnel_t, or_2_out);
  Multiplexer #(.select(3), .enable("false")) multiplexer_2 (
    .in0(alu_1_bit_1_salida), .in1(alu_1_bit_1_salida), .in2(alu_1_bit_1_salida), .in3(Salida[7]),
    .in4(tunnel_t_t), .in5(tunnel_t), .in6(alu_1_bit_1_salida), .in7(alu_1_bit_1_salida), .out(Salida[0]),
    .sel(\Operación ));
  or or_3 (or_3_out, Salida[7], tunnel_t);
  not not_5 (tunnel_t_t, or_3_out);

  // Other names for the same wires on the sheet: D[2:0] = \Operación ; P = \Operación [0]; tunnel = Salida[7]

  // Notes on the sheet:
  //   - And
  //   - Or
  //   - Not
  //   - Adición
  //   Notas:
  //   - Sustracción
  //   - Comparación
  //   Si es 0, entonces la premisa es falsa. Si es 1, es verdadera.
  //   Unidad Aritmético-Lógica (ALU) de 8-Bits con operaciones:
  //   En las comparaciones, el Bit Menos Significativo nos dice el resultado:
  //   Si hay Overflow en la resta, el resultado de las comparaciones puede no ser correcto.
  //   Códigos de las
  //   Operaciones
  //   000 - AND
  //   001 - OR
  //   010 - NOT
  //   011 - Menor que
  //   100 - Mayor que
  //   101 - Igualdad
  //   110 - Adición
  //   111 - Sustracción
endmodule
